// Logisim project Ctl_Load_Store.circ as structural Verilog: 1 circuit, main circuit Load_Store
module Load_Store (
  input  Enable,
  input  [15:0] Instruction,
  input  Clk,
  input  Reset,
  input  [31:0] Stack_Pointer,
  output [2:0] Rmd,
  output [31:0] RAM_Addr,
  output Store,
  output Load,
  output PC_Hold
);

  wire and_1_out, and_2_out, and_3_out, d_ff_1_q, d_ff_1_qn, not_1_out, not_2_out, or_1_out;
  wire [2:0] E3;
  wire [31:0] adder_1_out, E32, imm8;

  not not_1 (not_1_out, Instruction[11]);
  D_Flip_Flop #(.trigger("falling")) d_ff_1 (
    .D(and_1_out), .clk(Clk), .Q(d_ff_1_q), .Qn(d_ff_1_qn), .reset(or_1_out));  // open: preset
  and and_1 (and_1_out, ~d_ff_1_q, Instruction[11]);  // AND_Gate
  or or_1 (or_1_out, Reset, not_2_out);
  not not_2 (not_2_out, Enable);
  assign imm8 = {{24{Instruction[7]}}, Instruction[7:0]};  // Bit_Extender bit_extender_1
  and and_2 (and_2_out, d_ff_1_q, Instruction[11]);
  and and_3 (and_3_out, Instruction[11], d_ff_1_qn);
  and and_4 (Store, Enable, not_1_out);
  and and_5 (Load, Enable, and_2_out);
  and and_6 (PC_Hold, Enable, and_3_out);
  assign E3 = {{2{Enable}}, Enable};  // Bit_Extender bit_extender_2
  assign E32 = {{31{Enable}}, Enable};  // Bit_Extender bit_extender_3
  Adder #(.width(32)) adder_1 (.a(Stack_Pointer), .b(imm8), .out(adder_1_out));  // open: cin, cout
  assign Rmd = E3 & Instruction[10:8];  // AND_Gate and_7, 3 bits wide
  assign RAM_Addr = E32 & adder_1_out;  // AND_Gate and_8, 32 bits wide

  // Other names for the same wires on the sheet: E1 = Enable; Rt[2:0] = Instruction[10:8]; Inst = Instruction[11];
  //   SP[31:0] = Stack_Pointer

  // Notes on the sheet:
  //   Instruction: pull=down
  //   Delay load and hold PC for 1 cycle for the RAM to send out requested data 
endmodule
